# Fritzing sketch voltage divider 3_28_25 (saved by Fritzing 1.0.4)
breadboards: 1

parts:
  U1 = Voltage Regulator - 5V [package="TO220 [THT]"]
  C1 = Capacitor Polarized [package=panasonic_c]
  C2 = Capacitor Polarized [package=panasonic_c]
  Adafruit#1 = Adafruit ADS1115 16-Bit ADC [part_number=1085]  # not connected
  R2 = Basic Force Sensing Resistor (FSR) [package=THT]
  R1 = Resistor [tolerance=±5% power=0.25W resistance=220 package=THT]

nets:
  N1: U1.input_voltage, C1.-
  N2: U1.GND, C1.+, C2.-, R2.pin_2
  N3: U1.output_voltage, C2.+, R1.Pin_0
  N4: R2.pin_1, R1.Pin_1

custom parts:
  Adafruit ADS1115 16-Bit ADC: For microcontrollers without an analog-to-digital converter or when you want a higher-precision ADC, the ADS1115 provides 16-bit precision at 860 samples/second over I2C. The chip can be configured as 4 single-ended input channels, or two differential channels. As a nice bonus, it even includes a programmable gain amplifier, up to x16, to help boost up smaller single/differential signals to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
