# Fritzing sketch bender PCB (saved by Fritzing 1.0.3b)
circuit board: 11.203cm x 8.45681cm

parts:
  Adafruit_MCP3421_18-Bit_ADC1 = Adafruit MCP3421 18-Bit ADC [part_number=#5870]  # not connected
  Adafruit_Qwiic_/_Stemma_QT_5_Port_Hub1 = Adafruit Qwiic / Stemma QT 5 Port Hub [part_number=#5625]  # not connected
  Adafrit_Precision_Volt_Ref = Adafruit LM4040 Voltage Reference [part_number="Adafruit #2200"]
  R1 = Resistor [tolerance=±5% power=0.25W resistance=220 package=THT]
  J1 = Camdenboss CTB0158-2 [part_number=CTB0158-2 package=THT]
  5V = female pin header, 4 pins [form="♀ (female)"]
  GND = female pin header, 5 pins [form="♀ (female)"]
  Vin/GND/-S/+S = female pin header, 4 pins [form="♀ (female)"]
  Vout_/_GND = female pin header, 4 pins [form="♀ (female)"]  # not connected

nets:
  N1: Adafrit_Precision_Volt_Ref.VIN, 5V.pin1, 5V.pin2, 5V.pin3, 5V.pin4
  N2: Adafrit_Precision_Volt_Ref.GND, J1.pin2, GND.pin1, GND.pin2, GND.pin3, GND.pin4, GND.pin5, Vin/GND/-S/+S.pin2, Vin/GND/-S/+S.pin3
  N3: Adafrit_Precision_Volt_Ref.2.048V, R1.Pin_0
  N4: Adafrit_Precision_Volt_Ref.4.096V, Vin/GND/-S/+S.pin1
  N5: R1.Pin_1, J1.pin1, Vin/GND/-S/+S.pin4

custom parts:
  Adafruit MCP3421 18-Bit ADC: The Adafruit MCP3421 18-Bit ADC is a simple, inexpensive, and easy to use 18-bit, 240 SPS, single-channel ADC with an I2C interface that can run up to 3.4MHz clock rate. A perfect component whenever you need an ADC that has differential inputs, adjustable gain, and a built in precision/low-drift reference voltage. One of the trade-offs with getting 18-bit precision is that the ADC is not going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
  Adafruit Qwiic / Stemma QT 5 Port Hub: Qwiic, or STEMMA QT, is a very efficient way to quickly prototype an idea, but a lot of Qwiic/Stemma QT driver boards only have one port, and devices have two ports but that's only good for chaining. Maybe you want to reduce your I2C line capacitance by having a star formation instead of a looooong chain. Or maybe its just easier for your mechanical layout to have them closer to a central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
  Adafruit LM4040 Voltage Reference: How good is your multimeter really? Or maybe your analog converter needs a good reference? Or lets say you want to test your microcontroller's conversion accuracy & precision. If only you had a dependable, high precision, rock-solid voltage reference. Now you know why we made this very cute and useful little breakout board. It has two very high precision shunt-type voltage references with 750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
